// Digital circuit Counter.dig as structural Verilog
module Counter (
  input  clk,
  input  in_2,
  input  in_3,
  input  in_4,
  input  in_5,
  input  in_6,
  input  in_7,
  input  in_8
);

  wire and_1_out, jk_ff_as_1_nq, jk_ff_as_1_q, jk_ff_as_2_nq, jk_ff_as_2_q, jk_ff_as_3_nq, jk_ff_as_3_q,
       jk_ff_as_4_q, nand_1_out, not_1_out, xnor_1_out, xnor_2_out, xnor_3_out, xnor_4_out;

  xnor xnor_1 (xnor_1_out, in_5, jk_ff_as_4_q);
  xnor xnor_2 (xnor_2_out, in_6, jk_ff_as_3_q);
  xnor xnor_3 (xnor_3_out, in_7, jk_ff_as_2_q);
  xnor xnor_4 (xnor_4_out, in_8, jk_ff_as_1_q);
  nand nand_1 (nand_1_out, xnor_1_out, xnor_2_out, xnor_3_out, xnor_4_out);
  and and_1 (and_1_out, clk, in_3);
  not not_1 (not_1_out, nand_1_out);
  JK_FF_AS jk_ff_as_1 (
    .Set(in_4), .J(in_2), .C(and_1_out), .K(in_2), .Clr(not_1_out), .Q(jk_ff_as_1_q), .nQ(jk_ff_as_1_nq));
  LED O0 (.in(jk_ff_as_1_q));
  JK_FF_AS jk_ff_as_2 (
    .Set(in_4), .J(in_2), .C(jk_ff_as_1_nq), .K(in_2), .Clr(not_1_out), .Q(jk_ff_as_2_q), .nQ(jk_ff_as_2_nq));
  LED O1 (.in(jk_ff_as_2_q));
  JK_FF_AS jk_ff_as_3 (
    .Set(in_4), .J(in_2), .C(jk_ff_as_2_nq), .K(in_2), .Clr(not_1_out), .Q(jk_ff_as_3_q), .nQ(jk_ff_as_3_nq));
  LED O2 (.in(jk_ff_as_3_q));
  JK_FF_AS jk_ff_as_4 (
    .Set(in_4), .J(in_2), .C(jk_ff_as_3_nq), .K(in_2), .Clr(not_1_out), .Q(jk_ff_as_4_q));  // open: nQ
  LED O3 (.in(jk_ff_as_4_q));
endmodule
