// Digital circuit Mod 24.dig as structural Verilog
module Mod_24 (
  input  clk
);

  wire and_1_out, and_2_out, jk_ff_as_1_nq, jk_ff_as_1_q, jk_ff_as_2_nq, jk_ff_as_2_q, jk_ff_as_3_nq,
       jk_ff_as_3_q, jk_ff_as_4_nq, jk_ff_as_4_q, jk_ff_as_5_nq, jk_ff_as_5_q, not_1_out, not_2_out,
       or_1_out, or_2_out;

  JK_FF_AS jk_ff_as_1 (.J(1'b1), .C(clk), .K(1'b1), .Clr(or_1_out), .Q(jk_ff_as_1_q), .nQ(jk_ff_as_1_nq));  // open: Set
  JK_FF_AS jk_ff_as_2 (
    .J(1'b1), .C(jk_ff_as_1_nq), .K(1'b1), .Clr(or_1_out), .Q(jk_ff_as_2_q), .nQ(jk_ff_as_2_nq));  // open: Set
  JK_FF_AS jk_ff_as_3 (
    .J(1'b1), .C(jk_ff_as_2_nq), .K(1'b1), .Clr(or_1_out), .Q(jk_ff_as_3_q), .nQ(jk_ff_as_3_nq));  // open: Set
  JK_FF_AS jk_ff_as_4 (
    .J(1'b1), .C(jk_ff_as_3_nq), .K(1'b1), .Clr(or_1_out), .Q(jk_ff_as_4_q), .nQ(jk_ff_as_4_nq));  // open: Set
  or or_1 (or_1_out, or_2_out, and_1_out);
  not not_1 (not_1_out, jk_ff_as_1_q);
  and and_1 (and_1_out, jk_ff_as_4_q, not_2_out, jk_ff_as_2_q, not_1_out);
  not not_2 (not_2_out, jk_ff_as_3_q);
  JK_FF_AS jk_ff_as_5 (
    .J(1'b1), .C(jk_ff_as_4_nq), .K(1'b1), .Clr(or_2_out), .Q(jk_ff_as_5_q), .nQ(jk_ff_as_5_nq));  // open: Set
  buf or_2 (or_2_out, and_2_out);  // Or open: In_1
  and and_2 (and_2_out, jk_ff_as_5_q, jk_ff_as_2_q, jk_ff_as_1_q);
endmodule
