// Digital circuit Non Overlapping 101 sequence detector.dig as structural Verilog
module Non_Overlapping_101_sequence_detector (
  input  Load,
  input  in_2,
  input  in_3,
  input  in_4,
  input  in_5,
  input  in_6,
  input  CLK,
  input  in_8,
  input  in_9,
  input  in_10,
  input  in_11,
  input  in_12
);

  wire _10_bit_piso_1_p2, _7448_1_pin9, _7448_1_pin10, _7448_1_pin11, _7448_1_pin12, _7448_1_pin13,
       _7448_1_pin14, _7448_1_pin15, and_1_out, and_2_out, and_3_out, FF0_q, FF1_nq, FF1_q, mod_16_1_p4,
       mod_16_1_p5, mod_16_1_p6, mod_16_1_p7, not_1_out;

  // _10_bit_PISO _10_bit_piso_1: pin names not known; wires that end beside it: CLK, _10_bit_piso_1_p2, Load, in_8, in_2, in_9, in_3, in_10, in_4, in_11, in_5, in_12, in_6
  not not_1 (not_1_out, _10_bit_piso_1_p2);
  and and_1 (and_1_out, FF0_q, not_1_out);
  D_FF_AS FF1 (.Set(1'b0), .D(and_1_out), .C(CLK), .Clr(Load), .Q(FF1_q), .nQ(FF1_nq));
  and and_2 (and_2_out, FF1_nq, _10_bit_piso_1_p2);
  and and_3 (and_3_out, _10_bit_piso_1_p2, FF1_q);
  D_FF_AS FF0 (.Set(1'b0), .D(and_2_out), .C(CLK), .Clr(Load), .Q(FF0_q));  // open: nQ
  // Mod_16 mod_16_1: pin names not known; wires that end beside it: and_3_out, Load, 1'b1, mod_16_1_p4, mod_16_1_p5, mod_16_1_p6, mod_16_1_p7
  _7448 _7448_1 (
    .pin1(mod_16_1_p5), .pin2(mod_16_1_p6), .pin3(1'b1), .pin4(1'b1), .pin5(1'b1), .pin6(mod_16_1_p7),
    .pin7(mod_16_1_p4), .pin8(1'b0), .pin9(_7448_1_pin9), .pin10(_7448_1_pin10), .pin11(_7448_1_pin11),
    .pin12(_7448_1_pin12), .pin13(_7448_1_pin13), .pin14(_7448_1_pin14), .pin15(_7448_1_pin15), .pin16(1'b1));
  Seven_Seg seven_seg_1 (
    .a(_7448_1_pin13), .b(_7448_1_pin12), .c(_7448_1_pin11), .d(_7448_1_pin10), .e(_7448_1_pin9),
    .f(_7448_1_pin15), .g(_7448_1_pin14), .dp(1'b0));

  // Notes on the sheet:
  //   CLK: Hz: 2
endmodule
