// Digital circuit Number of 1's.dig as structural Verilog
module Number_of_1_s (
  input  I5,
  input  I4,
  input  I3,
  input  I2,
  input  I1,
  input  I0
);

  wire _7483_1_pin2, _7483_1_pin6, _7483_1_pin9, _7483_1_pin15, _7483_2_pin2, _7483_2_pin6, _7483_2_pin9;

  _7483 _7483_1 (
    .pin1(1'b0), .pin2(_7483_1_pin2), .pin3(I1), .pin4(I0), .pin5(1'b1), .pin6(_7483_1_pin6), .pin7(1'b0),
    .pin8(1'b0), .pin9(_7483_1_pin9), .pin10(I5), .pin11(I4), .pin12(1'b0), .pin13(I3), .pin14(1'b0),
    .pin15(_7483_1_pin15), .pin16(1'b0));
  _7483 _7483_2 (
    .pin1(1'b0), .pin2(_7483_2_pin2), .pin3(1'b0), .pin4(1'b0), .pin5(1'b1), .pin6(_7483_2_pin6),
    .pin7(_7483_1_pin15), .pin8(_7483_1_pin6), .pin9(_7483_2_pin9), .pin10(_7483_1_pin9),
    .pin11(_7483_1_pin2), .pin12(1'b0), .pin13(I2), .pin14(1'b0), .pin15(1'b0), .pin16(1'b0));
  LED S2 (.in(_7483_2_pin2));
  LED S1 (.in(_7483_2_pin6));
  LED S0 (.in(_7483_2_pin9));
endmodule
