// Digital circuit Serial Adder Moore.dig as structural Verilog
module Serial_Adder_Moore (
  input  _1_bit_A,
  input  _1_bit_B,
  input  CLK
);

  wire and_1_out, and_2_out, d_ff_as_1_q, d_ff_as_2_q, or_1_out, xor_1_out, xor_2_out;

  xor xor_1 (xor_1_out, _1_bit_A, _1_bit_B);
  and and_1 (and_1_out, _1_bit_A, _1_bit_B);
  xor xor_2 (xor_2_out, xor_1_out, d_ff_as_2_q);
  and and_2 (and_2_out, xor_1_out, d_ff_as_2_q);
  or or_1 (or_1_out, and_2_out, and_1_out);
  D_FF_AS d_ff_as_1 (.Set(1'b0), .D(xor_2_out), .C(CLK), .Clr(1'b0), .Q(d_ff_as_1_q));  // open: nQ
  D_FF_AS d_ff_as_2 (.Set(1'b0), .D(or_1_out), .C(CLK), .Clr(1'b0), .Q(d_ff_as_2_q));  // open: nQ
  LED Sum (.in(d_ff_as_1_q));
  LED Carry (.in(d_ff_as_2_q));
endmodule
